# Fritzing sketch transistor tester (saved by Fritzing 0.9.10b)
breadboards: 1

parts:
  Arduino_Uno = Arduino Uno (Rev3)
  R1 = Resistor [tolerance=±1% resistance=680 power=0.25 package=THT]
  R2 = Resistor [tolerance=±1% resistance=680 power=0.25 package=THT]
  R3 = Resistor [tolerance=±1% resistance=680 power=0.25 package=THT]
  R4 = Resistor [tolerance=±1% resistance=470k power=0.25 package=THT]
  R5 = Resistor [tolerance=±1% resistance=470k power=0.25 package=THT]
  R6 = Resistor [tolerance=±1% resistance=470k power=0.25 package=THT]
  HD44780_Screen_with_PCF8574 = pcf8574 io expansion board [package=THT]
  Encoder = KY-040 Rotary encoder [package="Breakout board"]

nets:
  TP1: Arduino_Uno.A0, R1.Pin_1, R4.Pin_0
  TP2: Arduino_Uno.A1, R2.Pin_1, R5.Pin_0
  TP3: Arduino_Uno.A2, R3.Pin_1, R6.Pin_0
  N1: Arduino_Uno.D8, R1.Pin_0
  N2: Arduino_Uno.D9_PWM, R4.Pin_1
  N3: Arduino_Uno.D10_PWM/SS, R2.Pin_0
  N4: Arduino_Uno.D11_PWM/MOSI, R5.Pin_1
  N5: Arduino_Uno.D12/MISO, R3.Pin_0
  N6: Arduino_Uno.D13/SCK, R6.Pin_1
  GND: Arduino_Uno.GND, HD44780_Screen_with_PCF8574.GND, Encoder.GND
  N7: Arduino_Uno.D0/RX, HD44780_Screen_with_PCF8574.SDA
  N8: Arduino_Uno.D1/TX, HD44780_Screen_with_PCF8574.SCL
  N9: Arduino_Uno.D2, Encoder.SW
  N10: Arduino_Uno.D3_PWM, Encoder.DT
  N11: Arduino_Uno.D4, Encoder.CLK
  3.3V: Arduino_Uno.3V3
  5V: Arduino_Uno.5V, HD44780_Screen_with_PCF8574.VCC, Encoder.Vcc

custom parts:
  pcf8574 io expansion board: pcf8574 io expansion board.
  KY-040 Rotary encoder: KY-040 Rotary Encoder with switch on breakout borad from AZ Delivery
